# Fritzing sketch placa (saved by Fritzing 0.9.3b)
circuit board: 7cm x 5cm
perfboards: 1

parts:
  Sensores_VEN = female pin header, 7 pins [form="♀ (female)"]
  PotMin = Trimpot-#3296-flat [package=3386u]
  PotMax = Trimpot-#3296-flat [package=3386u]
  Nano = Arduino Nano (Rev3.0)
  Sensores_BK = male pin header, 4 pins [form="♂ (male)"]
  Motor_Giro = male pin header, 2 pins [form="♂ (male)"]
  PonteH_Entrada = female pin header, 6 pins [form="♀ (female)"]
  IR = female pin header, 3 pins [form="♀ (female)"]
  Motor_Comp = male pin header, 3 pins [form="♂ (male)"]
  PonteH_Saida = single row smd female pin header, 4 pins [form="♀ (female)"]
  J3 = Camdenboss CTB0158-2 [part_number=CTB0158-2 package=THT]
  Motor_BK = female pin header, 3 pins [form="♀ (female)"]
  Display = female pin header, 4 pins [form="♀ (female)"]

nets (from the breadboard view):
  N1: Sensores_VEN.pin1, PotMin.CW, PotMax.CW, Nano.GND, Sensores_BK.pin4, PonteH_Entrada.pin3, IR.pin2, Motor_Comp.pin1, J3.pin1, Motor_BK.pin1, Display.pin4
  N2: Sensores_VEN.pin2, Nano.D9
  N3: Sensores_VEN.pin3, Nano.D10
  N4: Sensores_VEN.pin4, Nano.D11/MOSI
  N5: Sensores_VEN.pin5, Nano.A3
  N6: Sensores_VEN.pin6, PotMin.CCW, PotMax.CCW, Nano.VIN, PonteH_Entrada.pin4, IR.pin3, Motor_Comp.pin2, J3.pin2, Motor_BK.pin2
  N7: PotMin.WIPER, Nano.A7
  N8: PotMax.WIPER, Nano.A6
  N9: Nano.D2, PonteH_Entrada.pin2
  N10: Nano.D3, PonteH_Entrada.pin1
  N11: Nano.D4, Motor_BK.pin3
  N12: Nano.D5, Motor_Comp.pin3
  N13: Nano.D6, Sensores_BK.pin3
  N14: Nano.D7, Sensores_BK.pin2
  N15: Nano.D8, Sensores_BK.pin1
  N16: Nano.5V, Display.pin3
  N17: Nano.A5, Display.pin1
  N18: Nano.A4, Display.pin2
  N19: Nano.A2, IR.pin1
  N20: Motor_Giro.pin1, PonteH_Saida.pin1
  N21: Motor_Giro.pin2, PonteH_Saida.pin2

custom parts:
  Trimpot-#3296-flat: Bourns #3296 Square Trimpot 25 turn lying flat for low profile
