# Fritzing sketch _pcb (saved by Fritzing 0.9.3b)
circuit board: 6.10413cm x 5.33097cm

parts:
  J9 = female pin header, 1 pin [form="♀ (female)"]
  J10 = female pin header, 1 pin [form="♀ (female)"]
  J11 = female pin header, 1 pin [form="♀ (female)"]
  J12 = female pin header, 1 pin [form="♀ (female)"]
  J13 = female pin header, 1 pin [form="♀ (female)"]
  J15 = female pin header, 1 pin [form="♀ (female)"]
  J16 = female pin header, 1 pin [form="♀ (female)"]
  J17 = female pin header, 1 pin [form="♀ (female)"]
  J18 = female pin header, 1 pin [form="♀ (female)"]
  J19 = female pin header, 1 pin [form="♀ (female)"]
  J20 = female pin header, 1 pin [form="♀ (female)"]
  J21 = female pin header, 1 pin [form="♀ (female)"]
  J22 = female pin header, 1 pin [form="♀ (female)"]
  J23 = female pin header, 1 pin [form="♀ (female)"]
  J24 = female pin header, 1 pin [form="♀ (female)"]
  J25 = female pin header, 1 pin [form="♀ (female)"]
  J26 = female pin header, 1 pin [form="♀ (female)"]
  J27 = female pin header, 1 pin [form="♀ (female)"]
  J28 = female pin header, 1 pin [form="♀ (female)"]
  J29 = female pin header, 1 pin [form="♀ (female)"]
  J30 = female pin header, 1 pin [form="♀ (female)"]
  J31 = female pin header, 1 pin [form="♀ (female)"]
  J32 = female pin header, 1 pin [form="♀ (female)"]
  J33 = female pin header, 1 pin [form="♀ (female)"]
  J34 = female pin header, 1 pin [form="♀ (female)"]
  J35 = female pin header, 1 pin [form="♀ (female)"]
  J43 = female pin header, 1 pin [form="♀ (female)"]
  J44 = female pin header, 1 pin [form="♀ (female)"]
  J45 = female pin header, 1 pin [form="♀ (female)"]
  S1 = Pushbutton [package="[THT]"]
  LED7 = LED - 5mm [color="Red (633nm)" package="5 mm [THT]"]
  J49 = female pin header, 1 pin [form="♀ (female)"]
  J50 = female pin header, 1 pin [form="♀ (female)"]
  J51 = female pin header, 1 pin [form="♀ (female)"]
  Componente2 = NRF24L01+ Breakout Board
  C1 = Electrolytic Capacitor [capacitance=1µF package="100 mil [THT, electrolytic]"]
  R6 = Resistor [tolerance=±5% resistance=220 package=THT]
  S2 = Pushbutton [package="[THT]"]
  Componente1 = Arduino Ethernet Shield (Rev3)
  J52 = double row female pin header, 8 pins [form="♀ (female)"]  # not connected
  J54 = female pin header, 3 pins [form="♀ (female)"]
  J53 = female pin header, 4 pins [form="♀ (female)"]

nets:
  N1: J9.pin1, Componente2.CS, Componente1.D8
  N2: J10.pin1, Componente1.PWM_D9
  N3: J11.pin1, J22.pin1, Componente1.A5/SCL
  N4: J12.pin1, Componente1.AREF
  N5: J13.pin1, J24.pin1, Componente1.A4/SDA
  N6: J15.pin1, Componente1.D2, J53.pin3
  N7: J16.pin1, Componente1.RX/D0
  N8: J17.pin1, Componente1.PWM_D3, J54.pin1
  N9: J18.pin1, Componente1.TX/D1
  N10: J19.pin1, S2.Pin_3, S2.Pin_4, Componente1.SDCS
  N11: J20.pin1, Componente2.CE, Componente1.D7
  N12: J21.pin1, S1.Pin_3, S1.Pin_4, Componente1.PWM_D5
  N13: J23.pin1, Componente1.A3
  N14: J25.pin1, Componente1.A2
  N15: J26.pin1, Componente1.A1
  N16: J27.pin1, Componente1.A0
  N17: J28.pin1, Componente1.IOREF
  GND: J29.pin1, J32.pin1, S1.Pin_1, S1.Pin_2, J51.pin1, Componente2.GND, C1.-, R6.Pin_0, S2.Pin_1, S2.Pin_2, Componente1.GND, J54.pin3, J53.pin4
  N18: J30.pin1, Componente1.VIN
  N19: J31.pin1, Componente1.5V, J54.pin2, J53.pin1
  VCC: J33.pin1, Componente2.VCC, C1.+, Componente1.3V3
  N20: J34.pin1, Componente1.N/A
  N21: J35.pin1, Componente1.RESET
  N22: J43.pin1, Componente2.MISO, Componente1.PWM_D11
  N23: J44.pin1, Componente1.ETH_CS
  N24: J45.pin1, Componente2.SCK, Componente1.SPI/D13
  N25: LED7.cathode, R6.Pin_1
  N26: LED7.anode, J50.pin1, Componente1.PWM_D6
  N27: J49.pin1, Componente2.MOSI, Componente1.SPI/D12
