# Fritzing sketch pcb_presskill (saved by Fritzing 0.9.3b)
circuit board: 5.62877cm x 8.69066cm
breadboards: 1

parts:
  R1 = Resistor [tolerance=±5% resistance=220 package=THT]
  LED1 = LED - 5mm [color="Red (633nm)" package="5 mm [THT]"]
  S1 = Pushbutton [package="[THT]"]
  S2 = Pushbutton [package="[THT]"]
  S3 = Pushbutton [package="[THT]"]
  S4 = Pushbutton [package="[THT]"]
  S5 = Pushbutton [package="[THT]"]
  R2 = Resistor [tolerance=±5% resistance=220 package=THT]
  R3 = Resistor [tolerance=±5% resistance=220 package=THT]
  R4 = Resistor [tolerance=±5% resistance=220 package=THT]
  R5 = Resistor [tolerance=±5% resistance=220 package=THT]
  LED2 = LED - 5mm [color="Red (633nm)" package="5 mm [THT]"]
  LED3 = LED - 5mm [color="Red (633nm)" package="5 mm [THT]"]
  LED4 = LED - 5mm [color="Red (633nm)" package="5 mm [THT]"]
  R6 = Resistor [tolerance=±5% resistance=220 package=THT]
  R7 = Resistor [tolerance=±5% resistance=220 package=THT]
  R8 = Resistor [tolerance=±5% resistance=220 package=THT]
  R9 = Resistor [tolerance=±5% resistance=220 package=THT]
  J1 = female pin header, 19 pins [form="♀ (female)"]
  J2 = female pin header, 19 pins [form="♀ (female)"]
  SW1 = DIP SWITCH [package=dipswitch-02]
  SW3 = DIP SWITCH [package=dipswitch-02]
  buz1 = Piezo Buzzer
  S6 = Pushbutton [package="[THT]"]
  R10 = Resistor [tolerance=±5% resistance=220 package=THT]
  J3 = female pin header, 4 pins [form="♀ (female)"]

nets:
  N1: R1.Pin_0, R2.Pin_0, R3.Pin_0, R4.Pin_0, R5.Pin_0, J1.pin14, R10.Pin_0
  N2: R1.Pin_1, S4.Pin_1, S4.Pin_2, J1.pin7
  N3: LED1.cathode, R6.Pin_0
  N4: LED1.anode, J1.pin10
  N5: S1.Pin_1, S1.Pin_2, R2.Pin_1, J1.pin12
  N6: S1.Pin_3, S1.Pin_4, S2.Pin_3, S2.Pin_4, S3.Pin_3, S3.Pin_4, S4.Pin_3, S4.Pin_4, S5.Pin_1, S5.Pin_2, R6.Pin_1, R7.Pin_1, R8.Pin_1, R9.Pin_1, J1.pin19, S6.Pin_1, S6.Pin_2, J3.pin2
  N7: S2.Pin_1, S2.Pin_2, R3.Pin_1, J1.pin13
  N8: S3.Pin_1, S3.Pin_2, R4.Pin_1, J1.pin6
  N9: S5.Pin_3, S5.Pin_4, J2.pin16, R10.Pin_1
  N10: R5.Pin_1, J2.pin15, S6.Pin_3, S6.Pin_4
  N11: LED2.cathode, R7.Pin_0
  N12: LED2.anode, J1.pin11
  N13: LED3.cathode, R8.Pin_0
  N14: LED3.anode, J1.pin8
  N15: LED4.cathode, R9.Pin_0
  N16: LED4.anode, J1.pin9
  N17: J2.pin1, J3.pin1
  N18: J2.pin2, buz1.pin_1
  N19: J2.pin3, J3.pin4
  N20: J2.pin6, J3.pin3
  N21: J2.pin7, SW1.1, SW1.2, SW3.1, SW3.2, buz1.pin_2
  N22: J2.pin9, SW3.3
  N23: J2.pin10, SW3.4
  N24: J2.pin11, SW1.3
  N25: J2.pin12, SW1.4

custom parts:
  Piezo Buzzer: Part from https://www.nutsvolts.com/magazine/article/november2012_SmileysWorkshop modified to be .3 in spacing to match the adafruit buzzer 5V breadboard friendly part.
